// Logisim project alu-filp-flop.circ as structural Verilog: 1 circuit, main circuit main
module main (
);

  wire and_1_out, and_2_out, and_3_out, and_4_out, and_5_out, and_6_out, and_7_out, and_8_out, button_1_out,
       button_2_out, or_1_out, or_2_out, or_3_out, or_4_out, xor_1_out, xor_2_out, xor_4_out, xor_6_out,
       xor_8_out, xor_10_out, xor_11_out, xor_12_out, xor_13_out;
  wire [3:0] d_ff_1_q, xor_3_out;

  LED led_1 (.in(xor_1_out));
  xor xor_1 (xor_1_out, or_4_out, or_3_out);
  xor xor_2 (xor_2_out, d_ff_1_q[0], xor_10_out);
  and and_1 (and_1_out, d_ff_1_q[0], xor_10_out);
  xor xor_3 (xor_3_out[0], xor_2_out, 1'b0);
  and and_2 (and_2_out, d_ff_1_q[1], xor_11_out);
  xor xor_4 (xor_4_out, d_ff_1_q[1], xor_11_out);
  xor xor_5 (xor_3_out[1], xor_4_out, or_1_out);
  and and_3 (and_3_out, d_ff_1_q[2], xor_12_out);
  xor xor_6 (xor_6_out, d_ff_1_q[2], xor_12_out);
  xor xor_7 (xor_3_out[2], xor_6_out, or_2_out);
  and and_4 (and_4_out, d_ff_1_q[3], xor_13_out);
  xor xor_8 (xor_8_out, d_ff_1_q[3], xor_13_out);
  xor xor_9 (xor_3_out[3], xor_8_out, or_3_out);
  xor xor_10 (xor_10_out, 1'b1, 1'b0);
  xor xor_11 (xor_11_out, 1'b0, 1'b0);
  xor xor_12 (xor_12_out, 1'b1, 1'b0);
  xor xor_13 (xor_13_out, 1'b0, 1'b0);
  and and_5 (and_5_out, xor_2_out, 1'b0);
  or or_1 (or_1_out, and_1_out, and_5_out);
  and and_6 (and_6_out, xor_4_out, or_1_out);
  or or_2 (or_2_out, and_2_out, and_6_out);
  and and_7 (and_7_out, xor_6_out, or_2_out);
  or or_3 (or_3_out, and_3_out, and_7_out);
  and and_8 (and_8_out, xor_8_out, or_3_out);
  or or_4 (or_4_out, and_4_out, and_8_out);
  Button button_1 (.out(button_1_out));
  Hex_Digit_Display hex_digit_display_1 (.value(d_ff_1_q));  // open: dp
  D_Flip_Flop d_ff_1 (
    .clk(button_1_out), .D(xor_3_out[0]), .Q(d_ff_1_q[0]), .reset(button_2_out));  // open: Qn, preset, en
  D_Flip_Flop d_ff_2 (
    .clk(button_1_out), .D(xor_3_out[1]), .Q(d_ff_1_q[1]), .reset(button_2_out));  // open: Qn, preset, en
  D_Flip_Flop d_ff_3 (
    .clk(button_1_out), .D(xor_3_out[2]), .Q(d_ff_1_q[2]), .reset(button_2_out));  // open: Qn, preset, en
  D_Flip_Flop d_ff_4 (
    .clk(button_1_out), .D(xor_3_out[3]), .Q(d_ff_1_q[3]), .reset(button_2_out));  // open: Qn, preset, en
  Button button_2 (.out(button_2_out));

  // Notes on the sheet:
  //   2nd operand
  //   Overflow
  //   Result
  //   Subtract
  //   Increment
  //   Value
  //   Clear
endmodule
