// Logisim project alu.circ as structural Verilog: 1 circuit, main circuit main
module main (
);

  wire and_1_out, and_2_out, and_3_out, and_4_out, and_5_out, and_6_out, and_7_out, and_8_out, not_1_out,
       not_2_out, not_3_out, not_4_out, or_1_out, or_2_out, or_3_out, or_4_out, or_5_out, or_6_out, or_7_out,
       or_8_out, xor_1_out, xor_2_out, xor_3_out, xor_4_out, xor_5_out, xor_6_out, xor_7_out, xor_8_out,
       xor_9_out, xor_10_out, xor_11_out, xor_12_out, xor_13_out;
  wire [3:0] multiplexer_1_out;

  // Probe on 4'b0010
  // Probe on 4'b1101
  LED led_1 (.in(1'b1));
  LED led_2 (.in(1'b0));
  LED led_3 (.in(1'b1));
  LED led_4 (.in(1'b1));
  LED led_5 (.in(1'b0));
  LED led_6 (.in(1'b1));
  LED led_7 (.in(1'b0));
  LED led_8 (.in(1'b0));
  LED led_9 (.in(xor_1_out));
  xor xor_1 (xor_1_out, or_8_out, or_7_out);
  // Probe on multiplexer_1_out
  // Probe on multiplexer_1_out
  LED led_10 (.in(multiplexer_1_out[0]));
  LED led_11 (.in(multiplexer_1_out[1]));
  LED led_12 (.in(multiplexer_1_out[2]));
  LED led_13 (.in(multiplexer_1_out[3]));
  not not_1 (not_1_out, 1'b0);
  or or_1 (or_1_out, 1'b0, xor_10_out);
  not not_2 (not_2_out, 1'b1);
  or or_2 (or_2_out, 1'b1, xor_11_out);
  not not_3 (not_3_out, 1'b0);
  or or_3 (or_3_out, 1'b0, xor_12_out);
  not not_4 (not_4_out, 1'b0);
  or or_4 (or_4_out, 1'b0, xor_13_out);
  and and_1 (and_1_out, 1'b0, xor_10_out);
  xor xor_2 (xor_2_out, 1'b0, xor_10_out);
  xor xor_3 (xor_3_out, xor_2_out, 1'b0);
  Multiplexer #(.select(3), .disabled(0), .enable("false")) multiplexer_1 (
    .in0(or_1_out), .in1(not_1_out), .in2(and_1_out), .in3(xor_3_out), .in4(xor_2_out),
    .out(multiplexer_1_out[0]), .sel(3'b011));  // open: in5, in6, in7
  xor xor_4 (xor_4_out, 1'b1, xor_11_out);
  and and_2 (and_2_out, 1'b1, xor_11_out);
  xor xor_5 (xor_5_out, xor_4_out, or_5_out);
  Multiplexer #(.select(3), .disabled(0), .enable("false")) multiplexer_2 (
    .in0(or_2_out), .in1(not_2_out), .in2(and_2_out), .in3(xor_5_out), .in4(xor_4_out),
    .out(multiplexer_1_out[1]), .sel(3'b011));  // open: in5, in6, in7
  xor xor_6 (xor_6_out, 1'b0, xor_12_out);
  and and_3 (and_3_out, 1'b0, xor_12_out);
  xor xor_7 (xor_7_out, xor_6_out, or_6_out);
  Multiplexer #(.select(3), .disabled(0), .enable("false")) multiplexer_3 (
    .in0(or_3_out), .in1(not_3_out), .in2(and_3_out), .in3(xor_7_out), .in4(xor_6_out),
    .out(multiplexer_1_out[2]), .sel(3'b011));  // open: in5, in6, in7
  and and_4 (and_4_out, 1'b0, xor_13_out);
  xor xor_8 (xor_8_out, 1'b0, xor_13_out);
  xor xor_9 (xor_9_out, xor_8_out, or_7_out);
  Multiplexer #(.select(3), .disabled(0), .enable("false")) multiplexer_4 (
    .in0(or_4_out), .in1(not_4_out), .in2(and_4_out), .in3(xor_9_out), .in4(xor_8_out),
    .out(multiplexer_1_out[3]), .sel(3'b011));  // open: in5, in6, in7
  xor xor_10 (xor_10_out, 1'b1, 1'b0);
  xor xor_11 (xor_11_out, 1'b0, 1'b0);
  xor xor_12 (xor_12_out, 1'b1, 1'b0);
  xor xor_13 (xor_13_out, 1'b1, 1'b0);
  and and_5 (and_5_out, xor_2_out, 1'b0);
  or or_5 (or_5_out, and_1_out, and_5_out);
  and and_6 (and_6_out, xor_4_out, or_5_out);
  or or_6 (or_6_out, and_2_out, and_6_out);
  and and_7 (and_7_out, xor_6_out, or_6_out);
  or or_7 (or_7_out, and_3_out, and_7_out);
  and and_8 (and_8_out, xor_8_out, or_7_out);
  or or_8 (or_8_out, and_4_out, and_8_out);

  // Notes on the sheet:
  //   First operand
  //   2nd operand
  //   Overflow
  //   Result
  //   Opcode
  //   Subtract
endmodule
