// Logisim project array2x4.circ as structural Verilog: 1 circuit, main circuit main
module main (
);

  wire and_1_out, and_2_out, and_3_out, and_4_out, button_1_out, button_2_out, decoder_1_out0,
       decoder_1_out1, decoder_1_out2, decoder_1_out3, register_1_q, register_2_q, register_3_q,
       register_4_q, register_5_q, register_6_q, register_7_q, register_8_q;
  wire [1:0] multiplexer_1_out;
  wire [3:0] bit_extender_1_out;

  Button button_1 (.out(button_1_out));
  Button button_2 (.out(button_2_out));
  Register #(.width(1), .trigger("high")) register_1 (
    .D(1'b0), .Q(register_1_q), .clk(and_1_out), .clr(button_1_out));  // open: en
  Register #(.width(1), .trigger("high")) register_2 (
    .D(1'b1), .Q(register_2_q), .clk(and_1_out), .clr(button_1_out));  // open: en
  and and_1 (and_1_out, button_2_out, decoder_1_out0);
  Register #(.width(1), .trigger("high")) register_3 (
    .D(1'b0), .Q(register_3_q), .clk(and_2_out), .clr(button_1_out));  // open: en
  Register #(.width(1), .trigger("high")) register_4 (
    .D(1'b1), .Q(register_4_q), .clk(and_2_out), .clr(button_1_out));  // open: en
  and and_2 (and_2_out, button_2_out, decoder_1_out1);
  Decoder #(.select(2)) decoder_1 (
    .out0(decoder_1_out0), .out1(decoder_1_out1), .out2(decoder_1_out2), .out3(decoder_1_out3), .sel(2'b00));  // open: en
  Register #(.width(1), .trigger("high")) register_5 (
    .D(1'b0), .Q(register_5_q), .clk(and_3_out), .clr(button_1_out));  // open: en
  Register #(.width(1), .trigger("high")) register_6 (
    .D(1'b1), .Q(register_6_q), .clk(and_3_out), .clr(button_1_out));  // open: en
  and and_3 (and_3_out, button_2_out, decoder_1_out2);
  Register #(.width(1), .trigger("high")) register_7 (
    .D(1'b0), .Q(register_7_q), .clk(and_4_out), .clr(button_1_out));  // open: en
  Register #(.width(1), .trigger("high")) register_8 (
    .D(1'b1), .Q(register_8_q), .clk(and_4_out), .clr(button_1_out));  // open: en
  and and_4 (and_4_out, button_2_out, decoder_1_out3);
  Multiplexer #(.select(2)) multiplexer_1 (
    .in0(register_1_q), .in1(register_3_q), .in2(register_5_q), .in3(register_7_q),
    .out(multiplexer_1_out[0]), .sel(2'b00));  // open: en
  Multiplexer #(.select(2)) multiplexer_2 (
    .in0(register_2_q), .in1(register_4_q), .in2(register_6_q), .in3(register_8_q),
    .out(multiplexer_1_out[1]), .sel(2'b00));  // open: en
  Hex_Digit_Display hex_digit_display_1 (.value(bit_extender_1_out));  // open: dp
  assign bit_extender_1_out = {{2{1'b0}}, multiplexer_1_out};  // Bit_Extender bit_extender_1

  // Notes on the sheet:
  //   Data
  //   Clear
  //   WE
  //   Address
endmodule
