// Logisim project cmos.circ as structural Verilog: 1 circuit, main circuit main
module main (
);

  wire button_1_out, nand_1_out, not_1_out, transistor_1_out, transistor_3_out, transistor_5_out;

  Button button_1 (.out(button_1_out));
  Transistor transistor_1 (.in(1'b1), .out(transistor_1_out), .gate(button_1_out));
  LED led_1 (.in(transistor_1_out));
  Transistor #(.\type ("n")) transistor_2 (.in(1'b0), .out(transistor_1_out), .gate(button_1_out));
  LED led_2 (.in(not_1_out));
  not not_1 (not_1_out, button_1_out);
  Transistor transistor_3 (.in(1'b1), .out(transistor_3_out), .gate(1'b1));
  Transistor #(.\type ("n")) transistor_4 (.in(transistor_5_out), .out(transistor_3_out), .gate(1'b1));
  Transistor #(.\type ("n")) transistor_5 (.in(1'b0), .out(transistor_5_out), .gate(1'b1));
  nand nand_1 (nand_1_out, 1'b1, 1'b1);
  Transistor transistor_6 (.in(1'b1), .out(transistor_3_out), .gate(1'b1));
  LED led_3 (.in(transistor_3_out));
  LED led_4 (.in(nand_1_out));

  // Notes on the sheet:
  //   NOT
  //   NAND
endmodule
