// Logisim project counter.circ as structural Verilog: 1 circuit, main circuit main
module main (
);

  wire button_1_out, clock_1_out, t_ff_1_qn, t_ff_2_qn, t_ff_3_qn, t_ff_4_qn, t_ff_5_qn, t_ff_6_qn,
       t_ff_7_qn, t_ff_8_qn;
  wire [3:0] t_ff_1_q, t_ff_6_q;

  Clock clock_1 (.out(clock_1_out));
  Button button_1 (.out(button_1_out));
  T_Flip_Flop t_ff_1 (
    .clk(clock_1_out), .T(1'b1), .Q(t_ff_1_q[0]), .Qn(t_ff_1_qn), .reset(button_1_out));  // open: preset, en
  T_Flip_Flop t_ff_2 (
    .clk(t_ff_1_qn), .T(t_ff_1_qn), .Q(t_ff_1_q[1]), .Qn(t_ff_2_qn), .reset(button_1_out));  // open: preset, en
  Hex_Digit_Display hex_digit_display_1 (.value(t_ff_6_q));  // open: dp
  T_Flip_Flop t_ff_3 (
    .clk(t_ff_2_qn), .T(t_ff_2_qn), .Q(t_ff_1_q[2]), .Qn(t_ff_3_qn), .reset(button_1_out));  // open: preset, en
  Hex_Digit_Display hex_digit_display_2 (.value(t_ff_1_q));  // open: dp
  T_Flip_Flop t_ff_4 (
    .clk(t_ff_3_qn), .T(t_ff_3_qn), .Q(t_ff_1_q[3]), .Qn(t_ff_4_qn), .reset(button_1_out));  // open: preset, en
  T_Flip_Flop t_ff_5 (
    .clk(t_ff_6_qn), .T(t_ff_6_qn), .Q(t_ff_6_q[1]), .Qn(t_ff_5_qn), .reset(button_1_out));  // open: preset, en
  T_Flip_Flop t_ff_6 (
    .clk(t_ff_4_qn), .T(t_ff_4_qn), .Q(t_ff_6_q[0]), .Qn(t_ff_6_qn), .reset(button_1_out));  // open: preset, en
  T_Flip_Flop t_ff_7 (
    .clk(t_ff_5_qn), .T(t_ff_5_qn), .Q(t_ff_6_q[2]), .Qn(t_ff_7_qn), .reset(button_1_out));  // open: preset, en
  T_Flip_Flop t_ff_8 (
    .clk(t_ff_7_qn), .T(t_ff_7_qn), .Q(t_ff_6_q[3]), .Qn(t_ff_8_qn), .reset(button_1_out));  // open: preset, en
  LED led_1 (.in(t_ff_8_qn));

  // Notes on the sheet:
  //   Clear
endmodule
